// Logisim project J8.circ as structural Verilog: 1 circuit, main circuit main
module main (
  input  in_1,
  input  in_2,
  output out_3
);

  wire adder_1_out, and_1_out, not_1_out, or_1_out;

  not not_1 (not_1_out, in_1);
  and and_1 (and_1_out, in_1, in_2);
  or or_1 (or_1_out, in_1, in_2);
  Adder #(.width(1)) adder_1 (.a(in_1), .b(in_2), .out(adder_1_out));  // open: cin, cout
  Multiplexer #(.select(2), .enable("false")) multiplexer_1 (
    .in0(not_1_out), .in1(and_1_out), .in2(or_1_out), .in3(adder_1_out), .out(out_3));  // open: sel
endmodule
